# Fritzing sketch Harticle_Photom (saved by Fritzing 0.9.3b)
breadboards: 1

parts:
  TFT1 = 2.2" TFT with MicroSD Breakout
  J1 = longpad pin header, 13 pins [form="long pad"]
  Part4 = Photon

nets:
  N1: TFT1.BL, J1.pin3, Part4.A3
  N2: TFT1.MISO, J1.pin4, Part4.RST
  N3: TFT1.SCK, J1.pin5, Part4.D0
  N4: TFT1.MOSI, J1.pin6, Part4.A5
  N5: TFT1.CS, J1.pin7, Part4.A2
  N6: TFT1.SDCS, J1.pin8
  N7: TFT1.RST, J1.pin9
  N8: TFT1.VIN, J1.pin10
  N9: TFT1.GND, J1.pin11
  N10: J1.pin1, Part4.VIN
  N11: J1.pin2, Part4.GND

custom parts:
  2.2" TFT with MicroSD Breakout: 2.2" TFT Display with HX8340B Controller and MicroSD Card
